# Fritzing sketch Lab1 (saved by Fritzing 0.9.4)
breadboards: 1

parts:
  A1 = 7400 4 x 2 Input NAND Gate [part_number=7400 package="DIP (Dual Inline) [THT]"]
  B2 = 7400 4 x 2 Input NAND Gate [part_number=7400 package="DIP (Dual Inline) [THT]"]
  LED1 = LED - 5mm [color="Red (633nm)" package="5 mm [THT]"]
  B1 = 7400 4 x 2 Input NAND Gate [part_number=7400 package="DIP (Dual Inline) [THT]"]
  LED2 = LED - 5mm [color="Red (633nm)" package="5 mm [THT]"]

nets:
  A: A1.A1, B2.B3, B1.A1
  B: A1.B1, A1.A4, A1.B4, B1.B1, B1.A4, B1.B4
  N1: A1.Q1, A1.Q2
  N2: A1.A2, A1.A3
  Z-1: A1.B2, LED1.anode
  GND: A1.GND, B2.GND, LED1.cathode, B1.GND, LED2.cathode
  N3: A1.B3, A1.Q4
  C: A1.Q3, B2.Q3, B1.Q3
  5V: A1.VDD, B2.VDD, B1.VDD
  N4: B2.Q2, B1.B2
  N5: B2.B2, B2.B4
  N6: B2.A3, B2.A4
  Z-2: B2.Q4, LED2.anode
  N7: B1.Q1, B1.Q2
  N8: B1.A2, B1.A3
  N9: B1.B3, B1.Q4
